# Fritzing sketch EthernetClient (saved by Fritzing 0.9.2b)
breadboards: 1

parts:
  RHT1 = Humidity and Temperature Sensor RHT03
  Componente1 = Arduino Mega 2560 (Rev3)

nets:
  VCC: RHT1.Vcc, Componente1.3V3
  N1: RHT1.Data-signal, Componente1.D2_PWM
  N2: RHT1.GND_2, Componente1.GND

// code stored in the sketch: Untitled2.ino
/**
 Configura acesso a servidor PHP para envio de dados coletados de sensor de temperatura e umidade
 Intervalo de leitura: 5 minutos
 Forma de envio: HTML POST
 Formato da URL: http://localhost/arduinoServer/add.php
 Parametros do post: t=<temperatura em graus celsius>&u=<umidade relativa>
*/


#include <DHT.h>
#include <SPI.h>
#include <Ethernet.h>

// MAC address of the ethernet shield
byte mac[] = { 0x90, 0xA2, 0xDA, 0x0D, 0xA0, 0xF6 };
IPAddress ip(192, 168, 1, 20);
IPAddress dnsServer(192, 168, 1, 1);
IPAddress gateway(192, 168, 1, 1);
IPAddress subnet(255, 255, 255, 0);

byte serverAddress[] = {192, 168, 1, 111};
int serverPort = 80;

EthernetClient client;

#define DHTPIN 2
#define DHTTYPE DHT11    // SENSOR TYPE - THE ADAFRUIT LIBRARY OFFERS SUPPORT FOR MORE MODELS
DHT dht(DHTPIN, DHTTYPE);

long previousMillis = 0;
unsigned long currentMillis = 0;
long interval = 250000; // READING INTERVAL

int t = 0;	// TEMPERATURE VAR
int h = 0;	// HUMIDITY VAR
String data;
void setup() {
  Serial.begin(9600);
  Serial.println("Trying an ip from dhcp. Please, wait a moment.");
  //if (Ethernet.begin(mac) == 0) {
  //Serial.println("Failed to configure Ethernet using DHCP");
  // no point in carrying on, so do nothing forevermore:
  Ethernet.begin(mac, ip, dnsServer, gateway, subnet);
  //} else {
  //  Serial.println("Ethernet address defined successfully!");
  //}

  // print your local IP address:
  Serial.print("My IP address: ");
  for (byte thisByte = 0; thisByte < 4; thisByte++) {
    // print the value of each byte of the IP address:
    Serial.print(Ethernet.localIP()[thisByte], DEC);
    Serial.print(".");
  }
  Serial.println();

  dht.begin();
  delay(10000); // GIVE THE SENSOR SOME TIME TO START

  h = (int) dht.readHumidity();
  t = (int) dht.readTemperature();
  data = "";
}

String msg;
void loop() {

  currentMillis = millis();
  if (currentMillis - previousMillis > interval) { // READ ONLY ONCE PER INTERVAL
    previousMillis = currentMillis;
    h = (int) dht.readHumidity();
    t = (int) dht.readTemperature();
  }
  
  data = "t=" + String(t) + "&u=" + String(h);

  if (client.connect(serverAddress, serverPort)) {  // abre a conexao com o servidor

    client.println("POST /arduinoServer/add.php HTTP/1.1");
    msg = String("Host: ");
    for (byte thisByte = 0; thisByte < 4; thisByte++) {
      msg = msg + String(serverAddress[thisByte]);
    }
    client.println( msg );
    client.println("Content-Type: application/x-www-form-urlencoded");
    client.print("Content-Length: ");
    client.println( data.length() );
    client.println();
    client.println( data );
    
    Serial.print("Dados enviados: ");
    Serial.println(data);
  }

  if (client.connected()) {
    client.stop(); // encerra a conexão com o servidor
  }
  
  delay(5 * 60 * 1000); // WAIT FIVE MINUTES BEFORE SENDING AGAIN
}
